// Logisim project PROCESSORE.circ as structural Verilog: 1 circuit, main circuit main
module main (
  output [4:0] out_1,
  output [4:0] out_2,
  output [4:0] out_3,
  output [4:0] out_4,
  output [4:0] out_5
);

  wire and_1_out, and_2_out, and_3_out, and_4_out, and_6_out, \break , button_1_out, c, clear, COND,
       decoder_1_out0, decoder_1_out1, decoder_1_out2, decoder_1_out3, goto, \if , keyboard_1_avail, moove,
       multiplexer_2_out, not_1_out, not_2_out, not_3_out, \or , or_2_out, or_3_out, or_4_out, or_5_out,
       print, run_out, sel_data, shift_register_1_out, shift_register_2_q2, shift_register_2_q3,
       shift_register_2_q4, shift_register_2_q5, STAT, STAT1, W;
  wire [1:0] ir_r1;
  wire [2:0] ir_op_code;
  wire [4:0] alu_buffer_alu_out_4, ir_r2, multiplexer_7_out, multiplexer_8_out, xnor_1_out;
  wire [6:0] Data, ir_invio, memoria_out_6, multiplexer_5_out, multiplexer_6_out, print_buffer_out_4,
       rom_data;
  wire [7:0] adder_1_out, jump, multiplexer_1_out, multiplexer_3_out, PC, shifter_1_out, shifter_2_out;

  Button u_clear (.out(clear));
  Button run (.out(run_out));
  Keyboard keyboard_1 (.clk(c), .re(keyboard_1_avail), .avail(keyboard_1_avail), .data(Data));  // open: clr
  Clock clock_1 (.out(c));
  or or_1 (\or , clear, STAT1, run_out);
  or or_2 (or_2_out, run_out, \break );
  or or_3 (or_3_out, moove, sel_data);
  Multiplexer #(.width(8), .enable("false")) multiplexer_1 (
    .in0(8'h1), .in1(8'h6), .out(multiplexer_1_out), .sel(COND));
  Shift_Register #(.length(1)) shift_register_1 (
    .in(run_out), .clk(or_2_out), .out(shift_register_1_out), .clr(clear));  // open: shift, load, d0, q0
  Adder adder_1 (.a(PC), .b(multiplexer_1_out), .out(adder_1_out));  // open: cin, cout
  not not_1 (not_1_out, keyboard_1_avail);
  Multiplexer #(.enable("false")) multiplexer_2 (.in0(not_1_out), .in1(c), .out(multiplexer_2_out), .sel(or_4_out));
  or or_4 (or_4_out, shift_register_1_out, STAT);
  Multiplexer #(.width(8), .enable("false")) multiplexer_3 (
    .in0(adder_1_out), .in1(jump), .out(multiplexer_3_out), .sel(goto));
  Decoder #(.select(2), .enable("false")) decoder_1 (
    .out0(decoder_1_out0), .out1(decoder_1_out1), .out2(decoder_1_out2), .out3(decoder_1_out3), .sel(ir_r1));
  Register register_1 (.D(multiplexer_3_out), .Q(PC), .clk(multiplexer_2_out), .clr(\or ));  // open: en
  not not_2 (not_2_out, c);
  Shift_Register #(.length(6)) shift_register_2 (
    .in(print), .clk(c), .q2(shift_register_2_q2), .q3(shift_register_2_q3), .q4(shift_register_2_q4),
    .q5(shift_register_2_q5));  // open: shift, out, load, clr, d0, q0, d1, q1, d2, d3, d4, d5
  memoria_main memoria (.a(PC), .d(Data), .clock(c), .clear(clear), .store(keyboard_1_avail), .out_6(memoria_out_6));
  Multiplexer #(.width(5), .enable("false")) multiplexer_4 (
    .in0(ir_r2), .in1(alu_buffer_alu_out_4), .out(out_1), .sel(sel_data));
  and and_1 (and_1_out, or_3_out, not_2_out, decoder_1_out0);
  and and_2 (and_2_out, or_3_out, not_2_out, decoder_1_out1);
  and and_3 (and_3_out, or_3_out, not_2_out, decoder_1_out2);
  and and_4 (and_4_out, or_3_out, not_2_out, decoder_1_out3);
  stringtonum_main ir (.in_1(memoria_out_6), .clock(c), .op_code(ir_op_code), .r1(ir_r1), .r2(ir_r2), .invio(ir_invio));
  Register #(.width(5)) register_2 (.D(out_1), .Q(out_2), .clk(and_1_out), .clr(\or ));  // open: en
  Register #(.width(5)) register_3 (.D(out_1), .Q(out_3), .clk(and_2_out), .clr(\or ));  // open: en
  Register #(.width(5)) register_4 (.D(out_1), .Q(out_4), .clk(and_3_out), .clr(\or ));  // open: en
  Register #(.width(5)) register_5 (.D(out_1), .Q(out_5), .clk(and_4_out), .clr(\or ));  // open: en
  Multiplexer #(.width(7), .enable("false")) multiplexer_5 (
    .in0(Data), .in1(print_buffer_out_4), .out(multiplexer_5_out), .sel(or_5_out));
  or or_5 (or_5_out, shift_register_2_q5, shift_register_2_q4, shift_register_2_q3, shift_register_2_q2);
  numtustring_main print_buffer (.in_1(multiplexer_8_out), .print(print), .clo(c), .out_4(print_buffer_out_4));
  cu_main cu (
    .op_code(ir_op_code), .try(ir_invio), .select_data(sel_data), .\if (\if ), .goto(goto),
    .\break (\break ), .print(print), .write(W), .moove(moove));
  Multiplexer #(.width(7), .enable("false")) multiplexer_6 (
    .in0(multiplexer_5_out), .in1(rom_data), .out(multiplexer_6_out), .sel(STAT));
  TTY tty_1 (.data(multiplexer_6_out), .clk(c), .we(1'b1), .clr(\or ));
  Multiplexer #(.select(2), .width(5), .enable("false")) multiplexer_7 (
    .in0(out_2), .in1(out_3), .in2(out_4), .in3(out_5), .out(multiplexer_7_out), .sel(ir_r1));
  Multiplexer #(.select(2), .width(5), .enable("false")) multiplexer_8 (
    .in0(out_2), .in1(out_3), .in2(out_4), .in3(out_5), .out(multiplexer_8_out), .sel(ir_r2[1:0]));
  alu_main alu_buffer_alu (._1(multiplexer_7_out), ._2(multiplexer_8_out), .cl(sel_data), .out_4(alu_buffer_alu_out_4));
  Button button_1 (.out(button_1_out));
  Shifter shifter_1 (.in({3'b000, ir_r2}), .\dist (3'b010), .out(shifter_1_out));
  ROM_main rom (.PC(PC), .info(button_1_out), .clock(c), .STAT(STAT), .STAT1(STAT1), .DATA(rom_data));
  Shifter shifter_2 (.in({3'b000, ir_r2}), .\dist (3'b001), .out(shifter_2_out));
  assign xnor_1_out = ~(multiplexer_7_out ^ multiplexer_8_out);  // XNOR_Gate xnor_1, 5 bits wide
  Adder adder_2 (.a(shifter_2_out), .b(shifter_1_out), .out(jump));  // open: cin, cout
  and and_5 (COND, not_3_out, \if );
  not not_3 (not_3_out, and_6_out);
  and and_6 (and_6_out, xnor_1_out[4], xnor_1_out[3], xnor_1_out[2], xnor_1_out[1], xnor_1_out[0]);

  // Notes on the sheet:
  //   input
  //   buffer run
  //   pc
  //   registri
  //   output
  //   if condizione esegui successiva
  //   mult x6
endmodule
