// Logisim project ROM.circ as structural Verilog: 1 circuit, main circuit main
module main (
  input  [7:0] PC,
  input  info,
  input  clock,
  output STAT,
  output STAT1,
  output [6:0] DATA
);

  wire and_1_out, or_1_out, shift_register_1_q0, shift_register_1_q2;
  wire [6:0] xnor_1_out;

  Register #(.width(1)) register_1 (.D(info), .Q(STAT), .clk(or_1_out));  // open: en, clr
  and and_1 (and_1_out, xnor_1_out[6], xnor_1_out[5], xnor_1_out[4], xnor_1_out[3], xnor_1_out[2], xnor_1_out[1], xnor_1_out[0]);
  ROM #(.dataWidth(7)) rom_1 (.addr(PC), .data(DATA));  // open: sel
  or or_1 (or_1_out, info, shift_register_1_q0, shift_register_1_q2);
  Shift_Register #(.length(3)) shift_register_1 (
    .in(and_1_out), .clk(clock), .q0(shift_register_1_q0), .q2(shift_register_1_q2));  // open: shift, out, load, clr, d0, d1, q1, d2
  assign xnor_1_out = ~(DATA ^ 7'b0101110);  // XNOR_Gate xnor_1, 7 bits wide

  assign STAT1 = info;

  // Notes on the sheet:
  //   contents of rom_1 (hex, n*v repeats v):
  //   41 52 43 48 49 54 45 54 54 55 52 41 3a 20 4b 49 53 a 4d 45 4d 4f 52 49 41 3a 20 31 20 37 35 38 20 62
  //   69 74 a 50 52 4f 43 45 53 53 4f 52 45 3a 20 73 69 6e 67 6c 65 20 63 6f 72 65 40 34 2d 31 4b 48 7a a
  //   52 45 47 49 53 54 52 49 3a 20 30 2f 34 a 50 45 52 20 49 20 43 4f 4d 41 4e 44 49 20 43 4f 4e 53 55 4c
  //   54 41 52 45 20 4c 41 a 44 4f 43 55 4d 45 4e 54 41 5a 49 4f 4e 45 2e
endmodule
