// Logisim project alu.circ as structural Verilog: 1 circuit, main circuit main
module main (
  input  [4:0] _1,
  input  [4:0] _2,
  input  cl,
  output [4:0] out_4
);

  wire and_1_out, and_2_out, or_1_out;
  wire [3:0] adder_1_out, register_1_q;
  wire [4:0] register_2_q, subtractor_1_out;
  wire [4:4] register_1_q_2;

  Register #(.width(5)) register_1 (.D(_1), .Q({register_1_q_2[4], register_1_q}), .clk(cl));  // open: en, clr
  Register #(.width(5)) register_2 (.D(_2), .Q(register_2_q), .clk(cl));  // open: en, clr
  and and_1 (and_1_out, register_1_q_2[4], register_2_q[4]);
  and and_2 (and_2_out, ~register_2_q[4], ~register_1_q_2[4]);  // AND_Gate
  or or_1 (or_1_out, and_1_out, and_2_out);
  Adder #(.width(4)) adder_1 (.a(register_1_q), .b(register_2_q[3:0]), .out(adder_1_out));  // open: cin, cout
  Subtractor #(.width(5)) subtractor_1 (
    .a(register_2_q), .b({register_1_q_2[4], register_1_q}), .out(subtractor_1_out));  // open: bin, bout
  Multiplexer #(.width(5), .enable("false")) multiplexer_1 (
    .in0(subtractor_1_out), .in1({register_1_q_2[4], adder_1_out}), .out(out_4), .sel(or_1_out));
endmodule
