// Logisim project cu.circ as structural Verilog: 1 circuit, main circuit main
module main (
  input  [2:0] op_code,
  input  [6:0] try,
  output select_data,
  output \if ,
  output goto,
  output \break ,
  output print,
  output write,
  output moove
);

  and and_1 (write, ~try[0], try[1], ~try[2], try[3], ~try[4], ~try[5], ~try[6]);  // AND_Gate
  and m (moove, write, op_code[0], ~op_code[1], op_code[2]);  // AND_Gate
  and a (select_data, write, op_code[0], ~op_code[1], ~op_code[2]);  // AND_Gate
  and f (\if , write, ~op_code[0], op_code[1], op_code[2]);  // AND_Gate
  and g (goto, write, op_code[2], op_code[1], op_code[0]);
  and b (\break , ~op_code[0], op_code[1], ~op_code[2], write);  // AND_Gate
  and dis (print, ~op_code[0], ~op_code[1], op_code[2], write);  // AND_Gate
endmodule
