// Logisim project ir.circ as structural Verilog: 1 circuit, main circuit main
module main (
  input  [6:0] in_1,
  input  clock,
  output out_3,
  output [6:0] invio,
  output [6:0] r2,
  output [6:0] r1,
  output [6:0] op_code
);

  wire [6:1] shift_register_1_q2;

  Shift_Register #(.width(7), .length(6)) shift_register_1 (
    .in(in_1), .clk(clock), .q0(invio), .q1(r2), .q2({shift_register_1_q2, out_3}), .q3(r1), .q5(op_code));  // open: shift, out, load, clr, d0, d1, d2, d3, d4, q4, d5
endmodule
