// Logisim project memoria.circ as structural Verilog: 1 circuit, main circuit main
module main (
  input  [7:0] a,
  input  [6:0] d,
  input  clock,
  input  clear,
  input  store,
  output [6:0] out_6
);

  RAM #(.dataWidth(7), .bus("separate")) ram_1 (
    .addr(a), .din(d), .data(out_6), .str(store), .clk(clock), .clr(clear));  // open: sel, ld
endmodule
