// Logisim project numtustring.circ as structural Verilog: 1 circuit, main circuit main
module main (
  input  [4:0] in_1,
  input  print,
  input  clo,
  output [6:0] out_4
);

  wire not_1_out, not_2_out, shift_register_1_q0, shift_register_1_q1, shift_register_1_q2;
  wire [1:0] or_2_out;
  wire [6:0] multiplexer_1_out, multiplexer_3_out, register_1_q, register_2_q, register_3_q;
  wire [7:0] multiplexer_2_out;

  Multiplexer #(.width(7), .enable("false")) multiplexer_1 (
    .in0(7'b0110000), .in1(7'b0101101), .out(multiplexer_1_out), .sel(in_1[4]));
  Multiplexer #(.select(4), .width(8), .enable("false")) multiplexer_2 (
    .in0({8{1'b0}}), .in1(8'h1), .in2(8'h2), .in3(8'h3), .in4(8'h4), .in5(8'h5), .in6(8'h6), .in7(8'h7),
    .in8(8'h8), .in9(8'h9), .in10(8'h10), .in11(8'h11), .in12(8'h12), .in13(8'h13), .in14(8'h14),
    .in15(8'h15), .out(multiplexer_2_out), .sel(in_1[3:0]));
  Register #(.width(7)) register_1 (
    .D({3'b011, multiplexer_2_out[3:0]}), .Q(register_1_q), .clk(not_1_out));  // open: en, clr
  Register #(.width(7)) register_2 (
    .D({3'b011, multiplexer_2_out[7:4]}), .Q(register_2_q), .clk(not_1_out));  // open: en, clr
  Register #(.width(7)) register_3 (.D(multiplexer_1_out), .Q(register_3_q), .clk(not_1_out));  // open: en, clr
  not not_1 (not_1_out, print);
  Shift_Register #(.length(3)) shift_register_1 (
    .in(print), .clk(clo), .q0(shift_register_1_q0), .q1(shift_register_1_q1), .q2(shift_register_1_q2));  // open: shift, out, load, clr, d0, d1, d2
  Multiplexer #(.select(2), .width(7), .enable("false")) multiplexer_3 (
    .in0(7'b0001010), .in1(register_3_q), .in2(register_2_q), .in3(register_1_q), .out(multiplexer_3_out),
    .sel(or_2_out));
  or or_1 (or_2_out[1], shift_register_1_q2, shift_register_1_q1);
  or or_2 (or_2_out[0], shift_register_1_q0, shift_register_1_q2);
  Shift_Register #(.width(7), .length(3)) shift_register_2 (
    .in(multiplexer_3_out), .clk(not_2_out), .out(out_4));  // open: shift, load, clr, d0, q0, d1, q1, d2, q2
  not not_2 (not_2_out, clo);
endmodule
