// Logisim project stringtonum.circ as structural Verilog: 1 circuit, main circuit main
module main (
  input  [6:0] in_1,
  input  clock,
  output [2:0] op_code,
  output [1:0] r1,
  output [4:0] r2,
  output [6:0] invio
);

  wire [6:2] main_1_r1;
  wire [6:3] main_1_op_code;
  wire [6:4] main_1_r2;

  ir_main main_1 (
    .in_1(in_1), .clock(clock), .out_3(r2[4]), .invio(invio), .r2({main_1_r2, r2[3:0]}),
    .r1({main_1_r1, r1}), .op_code({main_1_op_code, op_code}));
endmodule
